# Fritzing sketch schematic (saved by Fritzing 0.9.3b)
breadboards: 1

parts:
  EMG_SENR = MyoWare Cable Shield
  ARDUINO_NANO = Arduino Nano (Rev3.0) (ICSP)
  SRV1 = Basic Servo
  SRV4 = Basic Servo
  SRV3 = Basic Servo
  SRV2 = Basic Servo
  SRV5 = Basic Servo
  VCC1 = Battery [part_number=6V]

nets:
  VCC: EMG_SENR.VCC, ARDUINO_NANO.3V3
  GND: EMG_SENR.GND, ARDUINO_NANO.GND
  N1: EMG_SENR.SIG, ARDUINO_NANO.A4
  N2: ARDUINO_NANO.D2, SRV1.pulse
  N3: ARDUINO_NANO.D3, SRV2.pulse
  N4: ARDUINO_NANO.D4, SRV3.pulse
  N5: ARDUINO_NANO.D5, SRV4.pulse
  N6: ARDUINO_NANO.D6, SRV5.pulse
  5V: ARDUINO_NANO.5V
  GND_2: SRV1.gnd, SRV4.gnd, SRV3.gnd, SRV2.gnd, SRV5.gnd, VCC1.-
  VCC_2: SRV1.vcc, SRV4.vcc, SRV3.vcc, SRV2.vcc, SRV5.vcc, VCC1.+

notes:
  U = 4 * 1,5 = 6 V
  3pmap, https://github.com/3PMAP, 2
