# Fritzing sketch FirstSetUp (saved by Fritzing 0.9.3b)
breadboards: 2

parts:
  Part9 = EasyDriver_v44
  Part10 = EasyDriver_v44
  M8 = Stepper Motor - Bipolar
  M12 = Stepper Motor - Bipolar
  Part13 = Arduino Nano (Rev3.0)
  J1 = Power Jack [package=power_jack_pth_lock]  # not connected
  Part14 = EasyDriver_v44
  Part15 = EasyDriver_v44
  M13 = Stepper Motor - Bipolar
  M14 = Stepper Motor - Bipolar

nets:
  GND: Part9.GND, Part10.GND
  N1: Part9.V+, Part10.V+
  N2: Part9.STEP, Part13.D2
  N3: Part9.DIR, Part13.D3
  N4: Part9.OUT2A, M12.A
  N5: Part9.OUT2B, M12.C
  N6: Part9.OUT1A, M12.D
  N7: Part9.OUT1B, M12.B
  N8: Part10.STEP, Part13.D4
  N9: Part10.DIR, Part13.D5
  N10: Part10.OUT2A, M8.A
  N11: Part10.OUT2B, M8.C
  N12: Part10.OUT1A, M8.D
  N13: Part10.OUT1B, M8.B
  N14: Part13.D6, Part15.STEP
  N15: Part13.D7, Part15.DIR
  N16: Part13.D8, Part14.STEP
  N17: Part13.D9, Part14.DIR
  GND_2: Part14.GND, Part15.GND
  N18: Part14.V+, Part15.V+
  N19: Part14.OUT2A, M13.A
  N20: Part14.OUT2B, M13.C
  N21: Part14.OUT1A, M13.D
  N22: Part14.OUT1B, M13.B
  N23: Part15.OUT2A, M14.A
  N24: Part15.OUT2B, M14.C
  N25: Part15.OUT1A, M14.D
  N26: Part15.OUT1B, M14.B

notes:
  Schematic 0.5:
  - 4 ipv 5 motortjes
  - 4 easydrivers
  - 2 per breadboard, dus 2 boards
  - van circuito.io
  - arduino zonder board?
  - aantal koppelingen ontbreken bij de arduino
  - niet getest
