# Fritzing sketch firstworking (saved by Fritzing 0.9.3b)
breadboards: 1

parts:
  ARDUINO_NANO = Arduino Nano (Rev3.0) (ICSP)
  DRV1 = X113647 Stepper Driver Board [package=board]
  MTR1 = 28BYJ-48 Stepper Motor
  LED1 = LED - 5mm [color="Yellow (595nm)" package="5 mm [THT]"]

nets:
  GND: ARDUINO_NANO.GND, DRV1.GND
  N1: ARDUINO_NANO.D8, DRV1.IN4
  N2: ARDUINO_NANO.D9, DRV1.IN3
  N3: ARDUINO_NANO.D10, DRV1.IN2
  N4: ARDUINO_NANO.D11/MOSI, DRV1.IN1
  N5: ARDUINO_NANO.5V, DRV1.+V
  N6: ARDUINO_NANO.3V3, LED1.anode
  N7: ARDUINO_NANO.D13/SCK, LED1.cathode
  N8: DRV1.BLUE, MTR1.BLUE
  N9: DRV1.PINK, MTR1.PINK
  N10: DRV1.YELLOW, MTR1.YELLOW
  N11: DRV1.ORANGE, MTR1.ORANGE
  N12: DRV1.RED, MTR1.RED

custom parts:
  X113647 Stepper Driver Board: A common stepper motor driver board based on ULN2003APG darlington array
  28BYJ-48 Stepper Motor: 28BYJ-48 gear-reduction stepper motor (small)
