# Fritzing sketch servo_driver_pcb (saved by Fritzing 0.9.3b)
circuit board: 2.76578cm x 5.77144cm
breadboards: 1

parts:
  SRV5 = Basic Servo
  -_+ = Battery [part_number=6V]
  SRV4 = Basic Servo
  SRV3 = Basic Servo
  SRV2 = Basic Servo
  SRV1 = Basic Servo
  SIG5 = male pin header, 1 pin [form="♂ (male)"]
  SIG4 = male pin header, 1 pin [form="♂ (male)"]
  SIG3 = male pin header, 1 pin [form="♂ (male)"]
  SIG2 = male pin header, 1 pin [form="♂ (male)"]
  SIG1 = male pin header, 1 pin [form="♂ (male)"]

nets:
  GND: SRV5.gnd, -_+.-, SRV4.gnd, SRV3.gnd, SRV2.gnd, SRV1.gnd
  VCC: SRV5.vcc, -_+.+, SRV4.vcc, SRV3.vcc, SRV2.vcc, SRV1.vcc
  N1: SRV5.pulse, SIG5.pin1
  N2: SRV4.pulse, SIG4.pin1
  N3: SRV3.pulse, SIG3.pin1
  N4: SRV2.pulse, SIG2.pin1
  N5: SRV1.pulse, SIG1.pin1

notes:
  https://github.com/bionicarm
  Servo driver
